# Fritzing sketch OdoTrip (saved by Fritzing 0.9.3b)
breadboards: 1

parts:
  U3 = SUP500F [package=sup500f]
  Componente1 = Arduino Nano (Rev3.0)
  Componente2 = Triple Axis Magnetometer - HMC5883 Breakout
  LCD1 = LCD 7Segmentos
  LCD2 = LCD 7Segmentos
  S1 = Pushbutton [package="[THT]"]
  S2 = Pushbutton [package="[THT]"]
  S3 = Pushbutton [package="[THT]"]
  R1 = Resistor [tolerance=±5% resistance=220 package=THT]
  R2 = Resistor [tolerance=±5% resistance=220 package=THT]
  R3 = Resistor [tolerance=±5% resistance=220 package=THT]

nets:
  GND: U3.GND, Componente1.GND, Componente2.GND, LCD1.GND, LCD2.GND
  N1: U3.TX, Componente1.D9
  N2: U3.RX, Componente1.D8
  VCC: U3.VCC, Componente1.5V, Componente2.VCC, LCD1.VCC, LCD2.VCC, S1.Pin_1, S1.Pin_2, S2.Pin_1, S2.Pin_2, S3.Pin_1, S3.Pin_2, R1.Pin_1, R2.Pin_1, R3.Pin_1
  N3: Componente1.D2, LCD1.CS
  N4: Componente1.D3, LCD1.WR
  N5: Componente1.D4, LCD1.Data
  N6: Componente1.D5, LCD2.CS
  N7: Componente1.D6, LCD2.WR
  N8: Componente1.D7, LCD2.Data
  N9: Componente1.D10, S3.Pin_3, S3.Pin_4, R3.Pin_0
  N10: Componente1.D11/MOSI, S2.Pin_3, S2.Pin_4, R1.Pin_0
  N11: Componente1.D12/MISO, S1.Pin_3, S1.Pin_4, R2.Pin_0
  N12: Componente1.A5, Componente2.SDA
  N13: Componente1.A4, Componente2.SCL

custom parts:
  SUP500F: SUP500F Venus GPS
  LCD 7Segmentos: A standard character display, usually with 2x16 characters. Comes in many colors.
